// Logisim project Yasiru_CPU.circ as structural Verilog: 1 circuit, main circuit main
module main (
  input  in_1,
  output [31:0] out_2
);

  wire clock_1_out, clock_2_out, clock_3_out, clock_4_out, decoder_1_out4, decoder_1_out5, decoder_1_out6,
       decoder_1_out7, decoder_2_out4, decoder_2_out5, decoder_2_out6, decoder_2_out7, JMPC, MEM_FT, MEM_R,
       MEM_W, not_1_out, not_2_out, not_3_out;
  wire [2:0] A_BUS_CTRL, B_BUS_CTRL;
  wire [5:0] ALU, C_BUS_CTRL;
  wire [7:0] controlled_buffer_1_out, main_2_out, MI_ADDR, MI_NX_ADDR, OP_CODE, RAM_D_OUT, register_2_q;
  wire [15:0] controlled_buffer_3_out;
  wire [22:21] register_1_q;
  wire [31:0] controlled_buffer_4_out, main_3_c, register_3_q, register_4_q, register_5_q, rom_1_data;
  wire [31:16] controlled_buffer_3_out_2;

  Pull_Resistor pull_resistor_1 (.node(MI_ADDR));
  ROM #(.dataWidth(32)) rom_1 (.addr(MI_ADDR), .data(rom_1_data), .sel(1'b1));
  Clock clock_1 (.out(clock_1_out));
  Multiplexer #(.width(8), .enable("false")) multiplexer_1 (.in0(OP_CODE), .in1(MI_NX_ADDR), .out(MI_ADDR), .sel(JMPC));
  Register #(.width(32)) register_1 (
    .D(rom_1_data), .en(1'b1),
    .Q({MI_NX_ADDR, JMPC, register_1_q, ALU, MEM_FT, MEM_R, MEM_W, A_BUS_CTRL, B_BUS_CTRL, C_BUS_CTRL}),
    .clk(clock_1_out), .clr(1'b0));
  Clock clock_2 (.out(clock_2_out));
  Register register_2 (.D(RAM_D_OUT), .en(1'b1), .Q(register_2_q), .clk(clock_2_out), .clr(1'b0));
  assign controlled_buffer_1_out = MEM_FT ? register_2_q : 8'bz;  // Controlled_Buffer controlled_buffer_1
  assign OP_CODE = not_1_out ? register_2_q : 8'bz;  // Controlled_Buffer controlled_buffer_2
  not not_1 (not_1_out, MEM_R);
  Clock clock_3 (.out(clock_3_out));
  shift_reg_main main_1 (.DIN(controlled_buffer_1_out), .CLK(clock_3_out), .EN(1'b1), .CLR(1'b0), .DOUT(out_2));
  assign {controlled_buffer_3_out_2, controlled_buffer_3_out} = decoder_1_out7 ? out_2 : 32'bz;  // Controlled_Buffer controlled_buffer_3
  assign controlled_buffer_4_out = decoder_2_out7 ? out_2 : 32'bz;  // Controlled_Buffer controlled_buffer_4
  not not_2 (not_2_out, MEM_R);
  Counter #(.width(16), .max('hffff)) counter_1 (
    .load(C_BUS_CTRL[2]), .D(main_3_c[15:0]), .count(not_2_out), .Q(controlled_buffer_3_out),
    .clk(clock_4_out), .clr(in_1));  // open: carry
  Register #(.width(32)) register_3 (.D(main_3_c), .en(C_BUS_CTRL[3]), .Q(register_3_q), .clk(clock_4_out), .clr(1'b0));
  Register #(.width(32)) register_4 (.D(main_3_c), .en(C_BUS_CTRL[4]), .Q(register_4_q), .clk(clock_4_out), .clr(1'b0));
  Register #(.width(32)) register_5 (.D(main_3_c), .en(C_BUS_CTRL[5]), .Q(register_5_q), .clk(clock_4_out), .clr(1'b0));
  Clock clock_4 (.out(clock_4_out));
  shitout_main main_2 (.IN(register_3_q), .CLK(clock_4_out), .CLR(C_BUS_CTRL[2]), .OUT(main_2_out));
  assign {controlled_buffer_3_out_2, controlled_buffer_3_out} = decoder_1_out4 ? register_3_q : 32'bz;  // Controlled_Buffer controlled_buffer_5
  assign controlled_buffer_4_out = decoder_2_out4 ? register_3_q : 32'bz;  // Controlled_Buffer controlled_buffer_6
  assign {controlled_buffer_3_out_2, controlled_buffer_3_out} = decoder_1_out5 ? register_4_q : 32'bz;  // Controlled_Buffer controlled_buffer_7
  assign controlled_buffer_4_out = decoder_2_out5 ? register_4_q : 32'bz;  // Controlled_Buffer controlled_buffer_8
  assign {controlled_buffer_3_out_2, controlled_buffer_3_out} = decoder_1_out6 ? register_5_q : 32'bz;  // Controlled_Buffer controlled_buffer_9
  assign controlled_buffer_4_out = decoder_2_out6 ? register_5_q : 32'bz;  // Controlled_Buffer controlled_buffer_10
  RAM #(.addrWidth(16), .bus("separate")) ram_1 (
    .addr(controlled_buffer_3_out), .din(main_2_out), .data(RAM_D_OUT), .str(MEM_W), .sel(1'b1),
    .clk(clock_4_out), .ld(not_3_out), .clr(1'b0));
  not not_3 (not_3_out, MEM_R);
  alu_main main_3 (
    .C(main_3_c), .A(controlled_buffer_4_out), .B({controlled_buffer_3_out_2, controlled_buffer_3_out}),
    .ALU_CTRL(ALU));
  Decoder #(.select(3), .disabled(0), .enable("false")) decoder_1 (
    .out4(decoder_1_out4), .out5(decoder_1_out5), .out6(decoder_1_out6), .out7(decoder_1_out7),
    .sel(B_BUS_CTRL));  // open: out0, out1, out2, out3
  Decoder #(.select(3), .disabled(0), .enable("false")) decoder_2 (
    .out4(decoder_2_out4), .out5(decoder_2_out5), .out6(decoder_2_out6), .out7(decoder_2_out7),
    .sel(A_BUS_CTRL));  // open: out0, out1, out2, out3
  // also tied to GND on the sheet: {controlled_buffer_3_out_2[16], controlled_buffer_3_out_2[17], controlled_buffer_3_out_2[18], controlled_buffer_3_out_2[19], controlled_buffer_3_out_2[20], controlled_buffer_3_out_2[21], controlled_buffer_3_out_2[22], controlled_buffer_3_out_2[23], controlled_buffer_3_out_2[24], controlled_buffer_3_out_2[25], controlled_buffer_3_out_2[26], controlled_buffer_3_out_2[27], controlled_buffer_3_out_2[28], controlled_buffer_3_out_2[29], controlled_buffer_3_out_2[30], controlled_buffer_3_out_2[31]}

  // Notes on the sheet:
  //   Micro Instuction Memory Module
  //   contents of rom_1 (hex, n*v repeats v):
  //   0 0 38c4000 4804000 5804000 6804000 70c0e20 0 9804000 a804000 b804000 c804000 a01d0 0 f1e0d60 0
  //   1f8d60 0 1f8ba0 0 0 0 178c4c08 18804000 19804000 1a804000 1b8c0e20 1c8a0010 1d8c2c04 1e801000
  //   1f801000 20801000 21801000 220c2a04
  //   MI REG
  //   MBR
  //   Memory Data Fetch Unit
  //   FT REG
  //   1 to write
  //   0 to read
  //   1 to fetch
  //   C BUS
  //   PC
  //   MDR
  //   B REG
  //   A REG
  //   Random Access Memory Module
  //   A BUS
  //   B BUS
endmodule
